// Logisim project NaveenRegister.circ as structural Verilog: 5 circuits, main circuit controller
module datapath (
  input  [31:0] W_Data,
  input  W_enable,
  input  [2:0] W_Addr,
  input  Choose_Display_Item,
  input  Reset,
  input  Start,
  output Lt_8
);

  wire Clear_A, Clear_B, Clear_C, Clear_D, CLK, Load_A, Load_B, Load_C, Load_D;
  wire [3:0] A_q, C_q, incrementer_1_plus_1, multiplexer_2_out, multiplexer_2_out_2, multiplexer_2_out_3,
       multiplexer_2_out_4, multiplexer_2_out_5, multiplexer_2_out_6, multiplexer_2_out_7,
       multiplexer_2_out_8;
  wire [31:0] B_q, D_q, Min_min_of_x_and_y_32_bits, multiplexer_1_out, Value1;

  Register #(.width(4)) C (.D(A_q), .en(Load_C), .Q(C_q), .clk(CLK), .clr(Clear_C));
  Clock clock_1 (.out(CLK));
  register_file register_file_1 (
    .Write_Data(W_Data), .Clock(CLK), .Write_Address(W_Addr), .Write_Enable(W_enable), .Read_Data(Value1),
    .Read_Address(C_q[2:0]), .Read_Enable(1'b1));
  Register #(.width(4)) A (.D(incrementer_1_plus_1), .en(Load_A), .Q(A_q), .clk(CLK), .clr(Clear_A));
  Comparator #(.width(4), .mode("unsigned")) comparator_1 (.a(A_q), .b(4'b1000), .lt(Lt_8));  // open: gt, eq
  incrementer incrementer_1 (.\input (A_q), .plus_1(incrementer_1_plus_1));
  controller controller_1 (
    .Clock(CLK), .lt(Lt_8), .Reset(Reset), .Start(Start), .A_Clear(Clear_A), .A_Load(Load_A),
    .B_Clear(Clear_B), .B_Load(Load_B), .C_Clear(Clear_C), .C_Load(Load_C), .D_Clear(Clear_D), .D_Load(Load_D));
  Register #(.width(32)) B (.D(multiplexer_1_out), .en(Load_B), .Q(B_q), .clk(CLK));  // open: clr
  Z_min_X_y__32_bits Min (
    .X_input_32_bits(B_q), .Y_input_32_bits(Value1), .Min_of_X_and_Y_32_bits(Min_min_of_x_and_y_32_bits));
  Multiplexer #(.width(32), .disabled(0), .enable("false")) multiplexer_1 (
    .in0(D_q), .in1({32{1'b1}}), .out(multiplexer_1_out), .sel(Clear_B));
  Register #(.width(32)) D (.D(Min_min_of_x_and_y_32_bits), .en(Load_D), .Q(D_q), .clk(CLK), .clr(Clear_D));
  Hex_Digit_Display hex_digit_display_1 (.value(multiplexer_2_out_8));  // open: dp
  Hex_Digit_Display hex_digit_display_2 (.value(multiplexer_2_out_7));  // open: dp
  Hex_Digit_Display hex_digit_display_3 (.value(multiplexer_2_out_6));  // open: dp
  Hex_Digit_Display hex_digit_display_4 (.value(multiplexer_2_out_5));  // open: dp
  Multiplexer #(.width(32), .disabled(0), .enable("false")) multiplexer_2 (
    .in0(W_Data), .in1(Value1),
    .out({multiplexer_2_out_8, multiplexer_2_out_7, multiplexer_2_out_6, multiplexer_2_out_5, multiplexer_2_out_4, multiplexer_2_out_3, multiplexer_2_out_2, multiplexer_2_out}),
    .sel(Choose_Display_Item));
  Hex_Digit_Display hex_digit_display_5 (.value(multiplexer_2_out_4));  // open: dp
  Hex_Digit_Display hex_digit_display_6 (.value(multiplexer_2_out_3));  // open: dp
  Hex_Digit_Display hex_digit_display_7 (.value(multiplexer_2_out));  // open: dp
  Hex_Digit_Display hex_digit_display_8 (.value(multiplexer_2_out_2));  // open: dp

  // Other names for the same wires on the sheet: Value0[31:0] = W_Data
endmodule

module controller (
  input  Clock,
  input  lt,
  input  Reset,
  input  Start,
  output A_Clear,
  output A_Load,
  output B_Clear,
  output B_Load,
  output C_Clear,
  output C_Load,
  output D_Clear,
  output D_Load
);

  wire State_0_p3, State_0_p4, State_0_p6, State_1_p3, State_1_p5, State_2_p3, State_4_p5, State_5_p3,
       State_5_p6;

  // StateMachine State_0: pin names not known; wires that end beside it: Clock, Reset, State_0_p3, State_0_p4, State_0_p4, State_0_p6, Start, A_Clear, C_Clear
  // StateMachine State_5: pin names not known; wires that end beside it: Clock, Reset, State_5_p3, State_5_p3, State_0_p6, State_5_p6
  // StateMachine State_1: pin names not known; wires that end beside it: Clock, 1'b0, State_1_p3, State_0_p3, State_1_p5, C_Load
  // StateMachine State_4: pin names not known; wires that end beside it: Clock, lt, State_5_p6, State_1_p5, State_4_p5, B_Load
  // StateMachine State_2: pin names not known; wires that end beside it: Clock, 1'b0, State_2_p3, State_1_p3, A_Load
  // StateMachine State_3: pin names not known; wires that end beside it: Clock, 1'b0, State_4_p5, State_2_p3, D_Load

  assign B_Clear = A_Clear;
  assign D_Clear = C_Clear;

  // Other names for the same wires on the sheet: Less_Than = lt
endmodule

module register_file (
  input  [31:0] Write_Data,
  input  Clock,
  input  [2:0] Read_Address,
  input  [2:0] Write_Address,
  input  Read_Enable,
  input  Write_Enable,
  output [31:0] Read_Data
);

  wire decoder_1_out0, decoder_1_out1, decoder_1_out2, decoder_1_out3, decoder_1_out4, decoder_1_out5,
       decoder_1_out6, decoder_1_out7, decoder_2_out0, decoder_2_out1, decoder_2_out2, decoder_2_out3,
       decoder_2_out4, decoder_2_out5, decoder_2_out6, decoder_2_out7;
  wire [31:0] register_1_q, register_2_q, register_3_q, register_4_q, register_5_q, register_6_q,
       register_7_q, register_8_q;

  Decoder #(.select(3), .disabled(0)) decoder_1 (
    .out0(decoder_1_out0), .out1(decoder_1_out1), .out2(decoder_1_out2), .out3(decoder_1_out3),
    .out4(decoder_1_out4), .out5(decoder_1_out5), .out6(decoder_1_out6), .out7(decoder_1_out7),
    .sel(Write_Address), .en(Write_Enable));
  assign Read_Data = decoder_2_out7 ? register_1_q : 32'bz;  // Controlled_Buffer controlled_buffer_1
  Register #(.width(32)) register_1 (.D(Write_Data), .en(decoder_1_out7), .Q(register_1_q), .clk(Clock));  // open: clr
  Register #(.width(32)) register_2 (.D(Write_Data), .en(decoder_1_out6), .Q(register_2_q), .clk(Clock));  // open: clr
  assign Read_Data = decoder_2_out6 ? register_2_q : 32'bz;  // Controlled_Buffer controlled_buffer_2
  Register #(.width(32)) register_3 (.D(Write_Data), .en(decoder_1_out5), .Q(register_3_q), .clk(Clock));  // open: clr
  assign Read_Data = decoder_2_out5 ? register_3_q : 32'bz;  // Controlled_Buffer controlled_buffer_3
  Register #(.width(32)) register_4 (.D(Write_Data), .en(decoder_1_out4), .Q(register_4_q), .clk(Clock));  // open: clr
  assign Read_Data = decoder_2_out4 ? register_4_q : 32'bz;  // Controlled_Buffer controlled_buffer_4
  assign Read_Data = decoder_2_out3 ? register_5_q : 32'bz;  // Controlled_Buffer controlled_buffer_5
  Register #(.width(32)) register_5 (.D(Write_Data), .en(decoder_1_out3), .Q(register_5_q), .clk(Clock));  // open: clr
  assign Read_Data = decoder_2_out2 ? register_6_q : 32'bz;  // Controlled_Buffer controlled_buffer_6
  Register #(.width(32)) register_6 (.D(Write_Data), .en(decoder_1_out2), .Q(register_6_q), .clk(Clock));  // open: clr
  assign Read_Data = decoder_2_out1 ? register_7_q : 32'bz;  // Controlled_Buffer controlled_buffer_7
  Register #(.width(32)) register_7 (.D(Write_Data), .en(decoder_1_out1), .Q(register_7_q), .clk(Clock));  // open: clr
  assign Read_Data = decoder_2_out0 ? register_8_q : 32'bz;  // Controlled_Buffer controlled_buffer_8
  Register #(.width(32)) register_8 (.D(Write_Data), .en(decoder_1_out0), .Q(register_8_q), .clk(Clock));  // open: clr
  Decoder #(.select(3), .disabled(0)) decoder_2 (
    .out0(decoder_2_out0), .out1(decoder_2_out1), .out2(decoder_2_out2), .out3(decoder_2_out3),
    .out4(decoder_2_out4), .out5(decoder_2_out5), .out6(decoder_2_out6), .out7(decoder_2_out7),
    .sel(Read_Address), .en(Read_Enable));
endmodule

module incrementer (
  input  [3:0] \input ,
  output [3:0] plus_1
);

  Adder #(.width(4)) adder_1 (.a(\input ), .b(4'b0001), .out(plus_1), .cin(1'b0));  // open: cout
endmodule

module Z_min_X_y__32_bits (
  input  [31:0] X_input_32_bits,
  input  [31:0] Y_input_32_bits,
  output [31:0] Min_of_X_and_Y_32_bits
);

  wire comparator_1_gt;

  Multiplexer #(.width(32)) multiplexer_1 (
    .in0(X_input_32_bits), .in1(Y_input_32_bits), .out(Min_of_X_and_Y_32_bits), .sel(comparator_1_gt),
    .en(1'b1));
  Comparator #(.width(32), .mode("unsigned")) comparator_1 (
    .a(X_input_32_bits), .b(Y_input_32_bits), .gt(comparator_1_gt));  // open: eq, lt
endmodule
